# Fritzing sketch TSL2591_NodeMCU (saved by Fritzing 0.9.3b)

parts:
  Part1 = Adafruit TSL2591 [part_number="Adafruit #1980"]
  U1 = NodeMCU V1.0
  LED1 = LEDs [package=led10mm]

nets:
  VIN: Part1.VIN, U1.3V3
  GND: Part1.GND, U1.GND, LED1.A
  N1: Part1.SDA, U1.D2
  N2: Part1.SCL, U1.D1
  N3: U1.D3, LED1.C

custom parts:
  Adafruit TSL2591: When the future is dazzlingly-bright, this ultra-high-range luminosity sensor will help you measure it. The TSL2591 luminosity sensor is an advanced digital light sensor, ideal for use in a wide range of light situations. Compared to low cost CdS cells, this sensor is more precise, allowing for exact lux calculations and can be configured for different gain/timing ranges to detect light ranges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
  NodeMCU V1.0: ESP8266 based NodeMCU
